# Fritzing sketch m2315 temperature humidty sensor and lcd panel sketch (saved by Fritzing 0.9.3b)
breadboards: 1

parts:
  Parça1 = Arduino Mega 2560 (Rev3)
  Parça2 = Humidity Temperature Sensor SHT15
  LCD1 = LCD screen  # not connected
  R1 = Resistor [tolerance=±5% resistance=6.8k package="1206 [SMD]"]
  R2 = Resistor [tolerance=±5% resistance=6.8k package="1206 [SMD]"]
  Parça3 = SparkFun RPI-1031 Tilt-a-Whirl Breakout [part_number=SEN-10621]

nets:
  N1: Parça1.D21/SCL, Parça1.SCL, Parça2.SCL, R1.Pin_0, Parça3.S2
  N2: Parça1.D20/SDA, Parça1.SDA, Parça2.SDA, R2.Pin_0, Parça3.S1
  VCC: Parça1.5V, Parça2.VCC, R1.Pin_1, R2.Pin_1, Parça3.VCC
  GND: Parça1.GND, Parça2.GND, Parça3.GND
